# Fritzing sketch caprometro (saved by Fritzing 0.9.3b)

parts:
  LCD1 = LCD screen
  Componente1 = Bare Conductive Touch Board
  R1 = Resistor [tolerance=±5% resistance=220 package=THT]
  J1 = Basic Servo

nets:
  GND: LCD1.VSS, LCD1.R/W, LCD1.LED-, Componente1.GND, R1.Pin_1, J1.gnd
  VDD: LCD1.VDD, LCD1.LED+, Componente1.5V, J1.vcc
  N1: LCD1.V0, R1.Pin_0
  N2: LCD1.RS, Componente1.A0
  N3: LCD1.E, Componente1.A1
  N4: LCD1.DB4, Componente1.A2
  N5: LCD1.DB5, Componente1.A3
  N6: LCD1.DB6, Componente1.A4
  N7: LCD1.DB7, Componente1.A5
  N8: Componente1.D10_PWM/A10_(MIDI), J1.pulse
